// Logisim project exp1_half_and_full_adder.circ as structural Verilog: 1 circuit, main circuit main
module main (
  input  HA_A,
  input  FA_A,
  input  HA_B,
  input  FA_B,
  input  FA_CIN,
  output HA_SUM,
  output FA_SUM,
  output HA_CARRY,
  output FA_COUT
);

  wire and_2_out, and_3_out, xor_2_out;

  xor xor_1 (HA_SUM, HA_A, HA_B);
  and and_1 (HA_CARRY, HA_A, HA_B);
  xor xor_2 (xor_2_out, FA_A, FA_B);
  and and_2 (and_2_out, FA_A, FA_B);
  xor xor_3 (FA_SUM, xor_2_out, FA_CIN);
  and and_3 (and_3_out, xor_2_out, FA_CIN);
  or or_1 (FA_COUT, and_2_out, and_3_out);

  // Notes on the sheet:
  //   PART A: HALF ADDER
  //   HALF ADDER TRUTH TABLE:
  //   A=0, B=0 -> SUM=0, CARRY=0
  //   A=0, B=1 -> SUM=1, CARRY=0
  //   A=1, B=0 -> SUM=1, CARRY=0
  //   A=1, B=1 -> SUM=0, CARRY=1
  //   EXPERIMENT 1: IMPLEMENTATION OF HALF ADDER & FULL ADDER
  //   Half Adder: Sum = A ^ B, Carry = A & B | Full Adder: 2 Half Adders + OR Gate
  //   PART B: FULL ADDER (2 HALF ADDERS + OR GATE)
  //   FULL ADDER TRUTH TABLE:
  //   Cin B A | SUM COUT | Cin B A | SUM COUT
  //    0  0 0 |  0    0   |  1  0 0 |  1    0 
  //    0  0 1 |  1    0   |  1  0 1 |  0    1 
  //    0  1 0 |  1    0   |  1  1 0 |  0    1 
  //    0  1 1 |  0    1   |  1  1 1 |  1    1 
endmodule
