// Logisim project exp2_mux_and_demux.circ as structural Verilog: 1 circuit, main circuit main
module main (
  input  I0,
  input  DEMUX_DIN,
  input  I1,
  input  I2,
  input  I3,
  input  MUX_S1,
  input  DEMUX_S1,
  input  MUX_S0,
  input  DEMUX_S0,
  output Y0,
  output Y1,
  output MUX_OUT,
  output Y2,
  output Y3
);

  wire and_1_out, and_2_out, and_3_out, and_4_out, not_1_out, not_2_out, not_3_out, not_4_out, or_1_out,
       or_2_out;

  not not_1 (not_1_out, MUX_S1);
  not not_2 (not_2_out, MUX_S0);
  and and_1 (and_1_out, I0, not_1_out, not_2_out);
  and and_2 (and_2_out, I1, not_1_out, MUX_S0);
  and and_3 (and_3_out, I2, MUX_S1, not_2_out);
  and and_4 (and_4_out, I3, MUX_S1, MUX_S0);
  or or_1 (or_1_out, and_1_out, and_2_out);
  or or_2 (or_2_out, and_3_out, and_4_out);
  or or_3 (MUX_OUT, or_1_out, or_2_out);
  not not_3 (not_3_out, DEMUX_S1);
  not not_4 (not_4_out, DEMUX_S0);
  and and_5 (Y0, DEMUX_DIN, not_3_out, not_4_out);
  and and_6 (Y1, DEMUX_DIN, not_3_out, DEMUX_S0);
  and and_7 (Y2, DEMUX_DIN, DEMUX_S1, not_4_out);
  and and_8 (Y3, DEMUX_DIN, DEMUX_S1, DEMUX_S0);

  // Notes on the sheet:
  //   PART A: 4-TO-1 MULTIPLEXER (DATA SELECTOR)
  //   4:1 MUX FUNCTION TABLE:
  //   S1=0, S0=0 -> Y = I0
  //   S1=0, S0=1 -> Y = I1
  //   S1=1, S0=0 -> Y = I2
  //   S1=1, S0=1 -> Y = I3
  //   EXPERIMENT 2: IMPLEMENTATION OF 4:1 MUX & 1:4 DEMUX
  //   Gate Level Design with Inverters, AND & OR Gates + Logisim Integrated Blocks
  //   PART B: 1-TO-4 DEMULTIPLEXER (DATA DISTRIBUTOR)
  //   1:4 DEMUX FUNCTION TABLE:
  //   S1=0, S0=0 -> Y0=Din, Y1=0, Y2=0, Y3=0
  //   S1=0, S0=1 -> Y0=0, Y1=Din, Y2=0, Y3=0
  //   S1=1, S0=0 -> Y0=0, Y1=0, Y2=Din, Y3=0
  //   S1=1, S0=1 -> Y0=0, Y1=0, Y2=0, Y3=Din
endmodule
