// Logisim project exp3_jk_and_d_flip_flop.circ as structural Verilog: 1 circuit, main circuit main
module main (
  input  J,
  input  K,
  input  D,
  input  CLR_JK__Async,
  input  CLR_D__Async,
  input  GATE_J,
  input  GATE_D,
  input  GATE_K,
  output Q_JK,
  output Q_D,
  output nQ_JK,
  output nQ_D,
  output GATE_Q_JK,
  output GATE_Q_D,
  output GATE_nQ_JK,
  output GATE_nQ_D
);

  wire CLK_D_out, CLK_JK_out, GATE_CLK_D_out, GATE_CLK_JK_out, nand_1_p4, nand_2_p4, nand_3_p2, nand_3_p3,
       nand_5_out, nand_6_out, nand_9_p3, nand_10_p2, nand_10_p3, not_1_out;

  Clock GATE_CLK_JK (.out(GATE_CLK_JK_out));
  Clock CLK_JK (.out(CLK_JK_out));
  // NAND_Gate nand_1: pin names not known; wires that end beside it: GATE_nQ_JK, GATE_J, GATE_CLK_JK_out, nand_1_p4
  // NAND_Gate nand_2: pin names not known; wires that end beside it: GATE_CLK_JK_out, GATE_K, GATE_Q_JK, nand_2_p4
  J_K_Flip_Flop #(.trigger("falling")) JK_FF (
    .J(J), .clk(CLK_JK_out), .K(K), .Q(Q_JK), .Qn(nQ_JK), .reset(CLR_JK__Async));  // open: preset, en
  // NAND_Gate nand_3: pin names not known; wires that end beside it: nand_1_p4, nand_3_p2, nand_3_p3
  not not_1 (not_1_out, GATE_CLK_JK_out);
  // NAND_Gate nand_4: pin names not known; wires that end beside it: nand_3_p3, nand_2_p4, nand_3_p2
  not nand_5 (nand_5_out, not_1_out);  // NAND_Gate
  not nand_6 (nand_6_out, not_1_out);  // NAND_Gate
  // NAND_Gate nand_7: pin names not known; wires that end beside it: nand_5_out, GATE_nQ_JK, GATE_Q_JK
  // NAND_Gate nand_8: pin names not known; wires that end beside it: GATE_Q_JK, nand_6_out, GATE_nQ_JK
  Clock CLK_D (.out(CLK_D_out));
  Clock GATE_CLK_D (.out(GATE_CLK_D_out));
  // NAND_Gate nand_9: pin names not known; wires that end beside it: GATE_D, GATE_CLK_D_out, nand_9_p3
  // NAND_Gate nand_10: pin names not known; wires that end beside it: GATE_CLK_D_out, nand_10_p2, nand_10_p3
  not not_2 (nand_10_p2, GATE_D);
  D_Flip_Flop #(.trigger("falling")) D_FF (
    .clk(CLK_D_out), .D(D), .Q(Q_D), .Qn(nQ_D), .reset(CLR_D__Async));  // open: preset, en
  // NAND_Gate nand_11: pin names not known; wires that end beside it: GATE_nQ_D, nand_9_p3, GATE_Q_D
  // NAND_Gate nand_12: pin names not known; wires that end beside it: GATE_Q_D, nand_10_p3, GATE_nQ_D

  // Notes on the sheet:
  //   PART A: J-K FLIP-FLOP (INTEGRATED COMPONENT)
  //   JK TRUTH TABLE:
  //   J=0, K=0 -> Hold | J=0, K=1 -> Reset (0)
  //   J=1, K=0 -> Set (1) | J=1, K=1 -> Toggle (~Q)
  //   CLR=1   -> Q = 0 (Asynchronous Override)
  //   PART C: GATE-LEVEL MASTER-SLAVE J-K FLIP-FLOP (NAND GATES)
  //   Master Stage (Active High CLK) + Slave Stage (Active Low CLK) - Free of Race Conditions
  //   EXPERIMENT 3: VERIFICATION OF JK & D FLIP-FLOPS
  //   Top: Integrated Library Flip-Flops | Bottom: Gate-Level Implementations (NAND Gates)
  //   PART B: D FLIP-FLOP (INTEGRATED COMPONENT)
  //   D TRUTH TABLE:
  //   CLK v, D=0 -> Q=0 | CLK v, D=1 -> Q=1
  //   No Clock   -> Q(t+1) = Q(t) (Hold)
  //   CLR=1      -> Q = 0 (Asynchronous Override)
  //   PART D: GATE-LEVEL CLOCKED D LATCH / FLIP-FLOP (NAND GATES)
  //   4 NAND Gates + Inverter: When CLK=1 Q follows D, When CLK=0 Q holds state
endmodule
