// Logisim project exp4_siso_and_pipo.circ as structural Verilog: 1 circuit, main circuit main
module main (
  input  SERIAL_IN,
  input  RESET_SISO,
  input  D3,
  input  D2,
  input  D1,
  input  D0,
  input  RESET_PIPO,
  output Q3,
  output Q2,
  output Q1,
  output Q0,
  output SERIAL_OUT,
  output PIPO_Q3,
  output PIPO_Q2,
  output PIPO_Q1,
  output PIPO_Q0
);

  wire CLK_PIPO_out, CLK_SISO_out;
  wire [3:0] undriven, undriven_2;

  Clock CLK_SISO (.out(CLK_SISO_out));
  Clock CLK_PIPO (.out(CLK_PIPO_out));
  D_Flip_Flop #(.trigger("falling")) FF3__Q3 (
    .clk(CLK_SISO_out), .D(SERIAL_IN), .Q(Q3), .reset(RESET_SISO));  // open: Qn, preset, en
  D_Flip_Flop #(.trigger("falling")) PIPO_FF3 (
    .clk(CLK_PIPO_out), .D(D3), .Q(PIPO_Q3), .reset(RESET_PIPO));  // open: Qn, preset, en
  D_Flip_Flop #(.trigger("falling")) FF2__Q2 (
    .clk(CLK_SISO_out), .D(Q3), .Q(Q2), .reset(RESET_SISO));  // open: Qn, preset, en
  D_Flip_Flop #(.trigger("falling")) PIPO_FF2 (
    .clk(CLK_PIPO_out), .D(D2), .Q(PIPO_Q2), .reset(RESET_PIPO));  // open: Qn, preset, en
  D_Flip_Flop #(.trigger("falling")) FF1__Q1 (
    .clk(CLK_SISO_out), .D(Q2), .Q(Q1), .reset(RESET_SISO));  // open: Qn, preset, en
  D_Flip_Flop #(.trigger("falling")) PIPO_FF1 (
    .clk(CLK_PIPO_out), .D(D1), .Q(PIPO_Q1), .reset(RESET_PIPO));  // open: Qn, preset, en
  D_Flip_Flop #(.trigger("falling")) FF0__Q0 (
    .clk(CLK_SISO_out), .D(Q1), .Q(Q0), .reset(RESET_SISO));  // open: Qn, preset, en
  D_Flip_Flop #(.trigger("falling")) PIPO_FF0 (
    .clk(CLK_PIPO_out), .D(D0), .Q(PIPO_Q0), .reset(RESET_PIPO));  // open: Qn, preset, en
  // Probe on {undriven[3:2], Q3, undriven[0]}
  // Probe on undriven_2

  assign SERIAL_OUT = Q0;

  // Notes on the sheet:
  //   EXPERIMENT 4: IMPLEMENTATION OF 4-BIT SISO & PIPO REGISTERS
  //   Serial-In Serial-Out (Cascade Shift) & Parallel-In Parallel-Out (Immediate Load)
  //   PART A: 4-BIT SERIAL-IN SERIAL-OUT (SISO) SHIFT REGISTER
  //   PART B: 4-BIT PARALLEL-IN PARALLEL-OUT (PIPO) REGISTER
endmodule
