// Logisim project exp5_4bit_ripple_counter_dff.circ as structural Verilog: 1 circuit, main circuit main
module main (
  input  RESET_UP__Clear,
  input  RESET_DOWN__Clear,
  output UP_Q0,
  output UP_Q1,
  output UP_Q2,
  output UP_Q3,
  output DN_Q0,
  output DN_Q1,
  output DN_Q2,
  output DN_Q3
);

  wire CLK_DOWN_out, CLK_UP_out, DN_FF0__LSB_qn, DN_FF1_qn, DN_FF2_qn, DN_FF3__MSB_qn, UP_FF0__LSB_qn,
       UP_FF1_qn, UP_FF2_qn, UP_FF3__MSB_qn;
  wire [3:0] undriven, undriven_2;

  Clock CLK_UP (.out(CLK_UP_out));
  Clock CLK_DOWN (.out(CLK_DOWN_out));
  D_Flip_Flop #(.trigger("falling")) UP_FF0__LSB (
    .clk(CLK_UP_out), .D(UP_FF0__LSB_qn), .Q(UP_Q0), .Qn(UP_FF0__LSB_qn), .reset(RESET_UP__Clear));  // open: preset, en
  D_Flip_Flop #(.trigger("falling")) DN_FF0__LSB (
    .clk(CLK_DOWN_out), .D(DN_FF0__LSB_qn), .Q(DN_Q0), .Qn(DN_FF0__LSB_qn), .reset(RESET_DOWN__Clear));  // open: preset, en
  D_Flip_Flop #(.trigger("falling")) UP_FF1 (
    .clk(UP_Q0), .D(UP_FF1_qn), .Q(UP_Q1), .Qn(UP_FF1_qn), .reset(RESET_UP__Clear));  // open: preset, en
  D_Flip_Flop #(.trigger("falling")) DN_FF1 (
    .clk(DN_FF0__LSB_qn), .D(DN_FF1_qn), .Q(DN_Q1), .Qn(DN_FF1_qn), .reset(RESET_DOWN__Clear));  // open: preset, en
  D_Flip_Flop #(.trigger("falling")) UP_FF2 (
    .clk(UP_Q1), .D(UP_FF2_qn), .Q(UP_Q2), .Qn(UP_FF2_qn), .reset(RESET_UP__Clear));  // open: preset, en
  D_Flip_Flop #(.trigger("falling")) DN_FF2 (
    .clk(DN_FF1_qn), .D(DN_FF2_qn), .Q(DN_Q2), .Qn(DN_FF2_qn), .reset(RESET_DOWN__Clear));  // open: preset, en
  D_Flip_Flop #(.trigger("falling")) UP_FF3__MSB (
    .clk(UP_Q2), .D(UP_FF3__MSB_qn), .Q(UP_Q3), .Qn(UP_FF3__MSB_qn), .reset(RESET_UP__Clear));  // open: preset, en
  D_Flip_Flop #(.trigger("falling")) DN_FF3__MSB (
    .clk(DN_FF2_qn), .D(DN_FF3__MSB_qn), .Q(DN_Q3), .Qn(DN_FF3__MSB_qn), .reset(RESET_DOWN__Clear));  // open: preset, en
  // Probe on undriven
  // Probe on undriven
  // Probe on undriven
  // Probe on undriven_2
  // Probe on undriven_2
  // Probe on undriven_2
  Hex_Digit_Display hex_digit_display_1 (.value(undriven));  // open: dp
  Hex_Digit_Display hex_digit_display_2 (.value(undriven_2));  // open: dp

  // Notes on the sheet:
  //   PART A: 4-BIT BINARY UP COUNTER (Counts 0 to 15, Next Clock = Q)
  //   PART B: 4-BIT BINARY DOWN COUNTER (Counts 15 to 0, Next Clock = ~Q)
  //   EXPERIMENT 5: 4-BIT ASYNCHRONOUS UP & DOWN RIPPLE COUNTERS (D FLIP-FLOPS)
  //   Pure D Flip-Flop Architecture (No Mux): Top = 4-Bit UP Counter (CLK = Q) | Bottom = 4-Bit DOWN Counter (CLK = ~Q)
endmodule
