// Logisim project exp6_2bit_alu.circ as structural Verilog: 1 circuit, main circuit main
module main (
  input  [1:0] OPERAND_A__2_bit,
  input  [1:0] OPERAND_B__2_bit,
  input  [1:0] ALU_SEL__2_bit,
  output ADD_CARRY,
  output [1:0] ALU_RESULT,
  output SUB_BORROW,
  output DIV_ZERO_ERR
);

  wire [1:0] adder_1_out, divider_1_out, divider_1_rem, subtractor_1_out;

  // Probe on OPERAND_A__2_bit
  // Probe on OPERAND_B__2_bit
  // Probe on ALU_SEL__2_bit
  Comparator #(.width(2)) comparator_1 (.a(OPERAND_B__2_bit), .b(2'b00), .eq(DIV_ZERO_ERR));  // open: gt, lt
  Adder #(.width(2)) adder_1 (
    .a(OPERAND_A__2_bit), .b(OPERAND_B__2_bit), .out(adder_1_out), .cout(ADD_CARRY));  // open: cin
  Subtractor #(.width(2)) subtractor_1 (
    .a(OPERAND_A__2_bit), .b(OPERAND_B__2_bit), .out(subtractor_1_out), .bout(SUB_BORROW));  // open: bin
  Divider #(.width(2)) divider_1 (
    .a(OPERAND_A__2_bit), .b(OPERAND_B__2_bit), .out(divider_1_out), .rem(divider_1_rem));  // open: upper
  // Probe on adder_1_out
  // Probe on subtractor_1_out
  // Probe on divider_1_out
  // Probe on divider_1_rem
  Multiplexer #(.select(2), .width(2), .enable("false")) multiplexer_1 (
    .in0(adder_1_out), .in1(subtractor_1_out), .in2(divider_1_out), .in3(divider_1_rem), .out(ALU_RESULT),
    .sel(ALU_SEL__2_bit));
  // Probe on ALU_RESULT
  // Probe on ALU_RESULT

  // Notes on the sheet:
  //   1. ADDER [00]
  //   2. SUBTRACTOR [01]
  //   3. DIVIDER [10 & 11]
  //   EXPERIMENT 6: 2-BIT ARITHMETIC LOGIC UNIT (ALU)
  //   Integrated Functional Units: Adder, Subtractor, Divider (Quotient & Remainder) via 4:1 MUX
  //   SEL 00: ADD (A + B) | SEL 01: SUB (A - B) | SEL 10: DIV QUOTIENT (A / B) | SEL 11: DIV REMAINDER (A % B)
endmodule
